# Fritzing sketch Anymotuino (saved by Fritzing 0.9.0b)
breadboards: 1

parts:
  Part1 = Arduino Pro Mini v13
  Part2 = Max Power IR LED Kit
  Part3 = IR Receiver Breakout [package=PCB]
  VCC1 = Battery

nets:
  VCC: Part1.VCC, Part2.VCC, Part3.VCC, VCC1.+
  GND: Part1.GND, Part2.GND, Part3.GND, VCC1.-
  N1: Part1.D6_PWM, Part3.OUT
  N2: Part1.D3_PWM, Part2.CONTROL

notes:
  Max IR
  IR Reader
  HM-10 BLE
  Arduino
  This photo contains the breakout board for the HM-10. It's not necessary in our case, so I added the connections directly to the pins.
  The board is with the front side up (antenna and chip visible)
